// Logisim project CRC.circ as structural Verilog: 2 circuits, main circuit CRC::divider
module CRC__divider (
  input  [3:0] Dividend,
  input  [3:0] Divisor,
  output out_3,
  output [2:0] out_4
);

  wire [3:0] and_1_out;
  wire [3:3] xor_1_out;

  assign and_1_out = {4{Dividend[3]}} & Divisor;  // AND_Gate and_1, 4 bits wide
  assign {xor_1_out[3], out_4} = and_1_out ^ Dividend;  // XOR_Gate xor_1, 4 bits wide

  assign out_3 = Dividend[3];
endmodule

module CRC (
  input  [7:0] in_1,
  input  [3:0] in_2,
  output [10:0] out_3
);

  wire [2:0] crc_divider_1_out_4, crc_divider_2_out_4, crc_divider_3_out_4, crc_divider_4_out_4,
       crc_divider_5_out_4, crc_divider_6_out_4, crc_divider_7_out_4;

  CRC__divider crc_divider_1 (.Dividend(in_1[7:4]), .Divisor(in_2), .out_4(crc_divider_1_out_4));  // open: out_3
  CRC__divider crc_divider_2 (
    .Dividend({crc_divider_1_out_4, in_1[3]}), .Divisor(in_2), .out_4(crc_divider_2_out_4));  // open: out_3
  CRC__divider crc_divider_3 (
    .Dividend({crc_divider_2_out_4, in_1[2]}), .Divisor(in_2), .out_4(crc_divider_3_out_4));  // open: out_3
  CRC__divider crc_divider_4 (
    .Dividend({crc_divider_3_out_4, in_1[1]}), .Divisor(in_2), .out_4(crc_divider_4_out_4));  // open: out_3
  CRC__divider crc_divider_5 (
    .Dividend({crc_divider_4_out_4, in_1[0]}), .Divisor(in_2), .out_4(crc_divider_5_out_4));  // open: out_3
  CRC__divider crc_divider_6 (
    .Dividend({crc_divider_5_out_4, 1'b0}), .Divisor(in_2), .out_4(crc_divider_6_out_4));  // open: out_3
  CRC__divider crc_divider_7 (
    .Dividend({crc_divider_6_out_4, 1'b0}), .Divisor(in_2), .out_4(crc_divider_7_out_4));  // open: out_3
  CRC__divider crc_divider_8 (
    .Dividend({crc_divider_7_out_4, 1'b0}), .Divisor(in_2), .out_4(out_3[2:0]));  // open: out_3

  assign out_3[10:3] = in_1;
endmodule
