// Logisim project GRF2.circ as structural Verilog: 7 circuits, main circuit 1GRF
module _1GRF (
  input  [31:0] Input,
  input  Reset,
  input  Clock,
  input  Read0_enable,
  input  Read1_enable,
  input  Write_enable,
  output [31:0] Output_0,
  output [31:0] Output_1
);

  wire [31:0] register_1_q;

  Register #(.width(32)) register_1 (.D(Input), .en(Write_enable), .Q(register_1_q), .clk(Clock), .clr(Reset));
  assign Output_0 = Read0_enable ? register_1_q : 32'bz;  // Controlled_Buffer controlled_buffer_1
  assign Output_1 = Read1_enable ? register_1_q : 32'bz;  // Controlled_Buffer controlled_buffer_2
endmodule

module _2GRF (
  input  [31:0] Input,
  input  Read0_enable,
  input  Read0_address,
  input  Read1_enable,
  input  Clock,
  input  Reset,
  input  Read1_address,
  input  Write_enable,
  input  Write_address,
  output [31:0] Output_0,
  output [31:0] Output_1
);

  wire decoder_1_out0, decoder_1_out1, decoder_2_out0, decoder_2_out1, decoder_3_out0, decoder_3_out1;

  Decoder #(.disabled(0)) decoder_1 (
    .out0(decoder_1_out0), .out1(decoder_1_out1), .sel(Read0_address), .en(Read0_enable));
  Decoder #(.disabled(0)) decoder_2 (
    .out0(decoder_2_out0), .out1(decoder_2_out1), .sel(Read1_address), .en(Read1_enable));
  Decoder #(.disabled(0)) decoder_3 (
    .out0(decoder_3_out0), .out1(decoder_3_out1), .sel(Write_address), .en(Write_enable));
  _1GRF u_1grf_1 (
    .Input(Input), .Read0_enable(decoder_1_out0), .Read1_enable(decoder_2_out0),
    .Write_enable(decoder_3_out0), .Output_0(Output_0), .Output_1(Output_1), .Clock(Clock), .Reset(Reset));
  _1GRF u_1grf_2 (
    .Input(Input), .Read0_enable(decoder_1_out1), .Read1_enable(decoder_2_out1),
    .Write_enable(decoder_3_out1), .Output_0(Output_0), .Output_1(Output_1), .Clock(Clock), .Reset(Reset));
endmodule

module _4GRF (
  input  [31:0] Input,
  input  Read0_enable,
  input  [1:0] Read0_address,
  input  Read1_enable,
  input  Clock,
  input  Reset,
  input  [1:0] Read1_address,
  input  Write_enable,
  input  [1:0] Write_address,
  output [31:0] Output_0,
  output [31:0] Output_1
);

  wire decoder_1_out0, decoder_1_out1, decoder_2_out0, decoder_2_out1, decoder_3_out0, decoder_3_out1;

  Decoder #(.disabled(0)) decoder_1 (
    .out0(decoder_1_out0), .out1(decoder_1_out1), .sel(Read0_address[0]), .en(Read0_enable));
  Decoder #(.disabled(0)) decoder_2 (
    .out0(decoder_2_out0), .out1(decoder_2_out1), .sel(Read1_address[0]), .en(Read1_enable));
  Decoder #(.disabled(0)) decoder_3 (
    .out0(decoder_3_out0), .out1(decoder_3_out1), .sel(Write_address[0]), .en(Write_enable));
  _2GRF u_2grf_1 (
    .Input(Input), .Read0_enable(decoder_1_out0), .Read0_address(Read0_address[1]),
    .Read1_enable(decoder_2_out0), .Read1_address(Read1_address[1]), .Write_enable(decoder_3_out0),
    .Write_address(Write_address[1]), .Output_0(Output_0), .Output_1(Output_1), .Clock(Clock), .Reset(Reset));
  _2GRF u_2grf_2 (
    .Input(Input), .Read0_enable(decoder_1_out1), .Read0_address(Read0_address[1]),
    .Read1_enable(decoder_2_out1), .Read1_address(Read1_address[1]), .Write_enable(decoder_3_out1),
    .Write_address(Write_address[1]), .Output_0(Output_0), .Output_1(Output_1), .Clock(Clock), .Reset(Reset));
endmodule

module _8GRF (
  input  [31:0] Input,
  input  Read0_enable,
  input  [2:0] Read0_address,
  input  Read1_enable,
  input  Clock,
  input  Reset,
  input  [2:0] Read1_address,
  input  Write_enable,
  input  [2:0] Write_address,
  output [31:0] Output_0,
  output [31:0] Output_1
);

  wire decoder_1_out0, decoder_1_out1, decoder_2_out0, decoder_2_out1, decoder_3_out0, decoder_3_out1;

  Decoder #(.disabled(0)) decoder_1 (
    .out0(decoder_1_out0), .out1(decoder_1_out1), .sel(Read0_address[0]), .en(Read0_enable));
  Decoder #(.disabled(0)) decoder_2 (
    .out0(decoder_2_out0), .out1(decoder_2_out1), .sel(Read1_address[0]), .en(Read1_enable));
  Decoder #(.disabled(0)) decoder_3 (
    .out0(decoder_3_out0), .out1(decoder_3_out1), .sel(Write_address[0]), .en(Write_enable));
  _4GRF u_4grf_1 (
    .Input(Input), .Read0_enable(decoder_1_out0), .Read0_address(Read0_address[2:1]),
    .Read1_enable(decoder_2_out0), .Read1_address(Read1_address[2:1]), .Write_enable(decoder_3_out0),
    .Write_address(Write_address[2:1]), .Output_0(Output_0), .Output_1(Output_1), .Clock(Clock), .Reset(Reset));
  _4GRF u_4grf_2 (
    .Input(Input), .Read0_enable(decoder_1_out1), .Read0_address(Read0_address[2:1]),
    .Read1_enable(decoder_2_out1), .Read1_address(Read1_address[2:1]), .Write_enable(decoder_3_out1),
    .Write_address(Write_address[2:1]), .Output_0(Output_0), .Output_1(Output_1), .Clock(Clock), .Reset(Reset));
endmodule

module _16GRF (
  input  [31:0] Input,
  input  Read0_enable,
  input  [3:0] Read0_address,
  input  Read1_enable,
  input  Clock,
  input  Reset,
  input  [3:0] Read1_address,
  input  Write_enable,
  input  [3:0] Write_address,
  output [31:0] Output_0,
  output [31:0] Output_1
);

  wire decoder_1_out0, decoder_1_out1, decoder_2_out0, decoder_2_out1, decoder_3_out0, decoder_3_out1;

  Decoder #(.disabled(0)) decoder_1 (
    .out0(decoder_1_out0), .out1(decoder_1_out1), .sel(Read0_address[0]), .en(Read0_enable));
  Decoder #(.disabled(0)) decoder_2 (
    .out0(decoder_2_out0), .out1(decoder_2_out1), .sel(Read1_address[0]), .en(Read1_enable));
  Decoder #(.disabled(0)) decoder_3 (
    .out0(decoder_3_out0), .out1(decoder_3_out1), .sel(Write_address[0]), .en(Write_enable));
  _8GRF u_8grf_1 (
    .Input(Input), .Read0_enable(decoder_1_out0), .Read0_address(Read0_address[3:1]),
    .Read1_enable(decoder_2_out0), .Read1_address(Read1_address[3:1]), .Write_enable(decoder_3_out0),
    .Write_address(Write_address[3:1]), .Output_0(Output_0), .Output_1(Output_1), .Clock(Clock), .Reset(Reset));
  _8GRF u_8grf_2 (
    .Input(Input), .Read0_enable(decoder_1_out1), .Read0_address(Read0_address[3:1]),
    .Read1_enable(decoder_2_out1), .Read1_address(Read1_address[3:1]), .Write_enable(decoder_3_out1),
    .Write_address(Write_address[3:1]), .Output_0(Output_0), .Output_1(Output_1), .Clock(Clock), .Reset(Reset));
endmodule

module GRF__helper (
  input  Enable,
  input  [4:0] addr,
  output _0_enable,
  output _1_enable,
  output _2_enable,
  output _4_enable,
  output _8_enable,
  output _16_enable,
  output _2_addr,
  output [1:0] _4_addr,
  output [2:0] _8_addr,
  output [3:0] _16_addr
);

  wire nor_1_out, nor_2_out, nor_3_out, nor_4_out, nor_5_out;

  nor nor_1 (nor_1_out, addr[0], addr[1], addr[2], addr[3], addr[4]);
  nor nor_2 (nor_2_out, addr[1], addr[2], addr[3], addr[4]);
  nor nor_3 (nor_3_out, addr[2], addr[3], addr[4]);
  nor nor_4 (nor_4_out, addr[3], addr[4]);
  nor nor_5 (nor_5_out, addr[4], addr[4]);
  and and_1 (_0_enable, Enable, nor_1_out);
  and and_2 (_1_enable, Enable, nor_2_out, addr[0]);
  and and_3 (_2_enable, Enable, nor_3_out, addr[1]);
  and and_4 (_4_enable, Enable, nor_4_out, addr[2]);
  and and_5 (_8_enable, Enable, nor_5_out, addr[3]);
  and and_6 (_16_enable, Enable, addr[4]);

  assign _2_addr = addr[0];
  assign _4_addr = addr[1:0];
  assign _8_addr = addr[2:0];
  assign _16_addr = addr[3:0];

  // Notes on the sheet:
  //   Enable: pull=up
endmodule

module GRF (
  input  [31:0] Input,
  input  [4:0] Read0_address,
  input  [4:0] Read1_address,
  input  Write_enable,
  input  [4:0] Write_address,
  input  Reset,
  input  Clock,
  output [31:0] Output_0,
  output [31:0] Output_1
);

  wire grf_helper_1__1_enable, grf_helper_1__2_addr, grf_helper_1__2_enable, grf_helper_1__4_enable,
       grf_helper_1__8_enable, grf_helper_1__16_enable, grf_helper_2__0_enable, grf_helper_2__1_enable,
       grf_helper_2__2_addr, grf_helper_2__2_enable, grf_helper_2__4_enable, grf_helper_2__8_enable,
       grf_helper_2__16_enable, grf_helper_3__0_enable, grf_helper_3__1_enable, grf_helper_3__2_addr,
       grf_helper_3__2_enable, grf_helper_3__4_enable, grf_helper_3__8_enable, grf_helper_3__16_enable;
  wire [1:0] grf_helper_1__4_addr, grf_helper_2__4_addr, grf_helper_3__4_addr;
  wire [2:0] grf_helper_1__8_addr, grf_helper_2__8_addr, grf_helper_3__8_addr;
  wire [3:0] grf_helper_1__16_addr, grf_helper_2__16_addr, grf_helper_3__16_addr;

  GRF__helper grf_helper_1 (
    .addr(Write_address), ._1_enable(grf_helper_1__1_enable), ._2_enable(grf_helper_1__2_enable),
    ._4_enable(grf_helper_1__4_enable), ._8_enable(grf_helper_1__8_enable),
    ._16_enable(grf_helper_1__16_enable), ._2_addr(grf_helper_1__2_addr), ._4_addr(grf_helper_1__4_addr),
    ._8_addr(grf_helper_1__8_addr), ._16_addr(grf_helper_1__16_addr), .Enable(Write_enable));  // open: _0_enable
  GRF__helper grf_helper_2 (
    .addr(Read0_address), ._0_enable(grf_helper_2__0_enable), ._1_enable(grf_helper_2__1_enable),
    ._2_enable(grf_helper_2__2_enable), ._4_enable(grf_helper_2__4_enable),
    ._8_enable(grf_helper_2__8_enable), ._16_enable(grf_helper_2__16_enable), ._2_addr(grf_helper_2__2_addr),
    ._4_addr(grf_helper_2__4_addr), ._8_addr(grf_helper_2__8_addr), ._16_addr(grf_helper_2__16_addr));  // open: Enable
  GRF__helper grf_helper_3 (
    .addr(Read1_address), ._0_enable(grf_helper_3__0_enable), ._1_enable(grf_helper_3__1_enable),
    ._2_enable(grf_helper_3__2_enable), ._4_enable(grf_helper_3__4_enable),
    ._8_enable(grf_helper_3__8_enable), ._16_enable(grf_helper_3__16_enable), ._2_addr(grf_helper_3__2_addr),
    ._4_addr(grf_helper_3__4_addr), ._8_addr(grf_helper_3__8_addr), ._16_addr(grf_helper_3__16_addr));  // open: Enable
  _1GRF u_1grf_1 (
    .Read0_enable(grf_helper_2__0_enable), .Read1_enable(grf_helper_3__0_enable), .Output_0(Output_0),
    .Output_1(Output_1));  // open: Input, Write_enable, Clock, Reset
  _1GRF u_1grf_2 (
    .Input(Input), .Read0_enable(grf_helper_2__1_enable), .Read1_enable(grf_helper_3__1_enable),
    .Write_enable(grf_helper_1__1_enable), .Output_0(Output_0), .Output_1(Output_1), .Clock(Clock),
    .Reset(Reset));
  _2GRF u_2grf_1 (
    .Input(Input), .Read0_enable(grf_helper_2__2_enable), .Read0_address(grf_helper_2__2_addr),
    .Read1_enable(grf_helper_3__2_enable), .Read1_address(grf_helper_3__2_addr),
    .Write_enable(grf_helper_1__2_enable), .Write_address(grf_helper_1__2_addr), .Output_0(Output_0),
    .Output_1(Output_1), .Clock(Clock), .Reset(Reset));
  _4GRF u_4grf_1 (
    .Input(Input), .Read0_enable(grf_helper_2__4_enable), .Read0_address(grf_helper_2__4_addr),
    .Read1_enable(grf_helper_3__4_enable), .Read1_address(grf_helper_3__4_addr),
    .Write_enable(grf_helper_1__4_enable), .Write_address(grf_helper_1__4_addr), .Output_0(Output_0),
    .Output_1(Output_1), .Clock(Clock), .Reset(Reset));
  _8GRF u_8grf_1 (
    .Input(Input), .Read0_enable(grf_helper_2__8_enable), .Read0_address(grf_helper_2__8_addr),
    .Read1_enable(grf_helper_3__8_enable), .Read1_address(grf_helper_3__8_addr),
    .Write_enable(grf_helper_1__8_enable), .Write_address(grf_helper_1__8_addr), .Output_0(Output_0),
    .Output_1(Output_1), .Clock(Clock), .Reset(Reset));
  _16GRF u_16grf_1 (
    .Input(Input), .Read0_enable(grf_helper_2__16_enable), .Read0_address(grf_helper_2__16_addr),
    .Read1_enable(grf_helper_3__16_enable), .Read1_address(grf_helper_3__16_addr),
    .Write_enable(grf_helper_1__16_enable), .Write_address(grf_helper_1__16_addr), .Output_0(Output_0),
    .Output_1(Output_1), .Clock(Clock), .Reset(Reset));
endmodule
