// Logisim project fsm.circ as structural Verilog: 3 circuits, main circuit fsm::next_state_logic
module fsm__next_state_logic (
  input  i1,
  input  i0,
  input  d1,
  input  d0,
  output n1,
  output n0
);

  wire and_1_out, and_2_out, and_3_out, and_4_out, and_5_out, and_6_out, and_7_out, and_8_out, not_1_out,
       not_2_out, not_3_out, not_4_out, not_5_out, not_6_out, not_7_out, not_8_out, not_9_out, not_10_out,
       not_11_out, not_12_out, not_13_out, not_14_out, not_15_out, not_16_out;

  not not_1 (not_1_out, i1);
  and and_1 (and_1_out, not_1_out, i0, not_2_out);
  not not_2 (not_2_out, d1);
  not not_3 (not_3_out, i1);
  and and_2 (and_2_out, not_3_out, i0, not_4_out);
  not not_4 (not_4_out, d0);
  and and_3 (and_3_out, i1, not_5_out, not_6_out);
  not not_5 (not_5_out, i0);
  not not_6 (not_6_out, d1);
  not not_7 (not_7_out, i0);
  and and_4 (and_4_out, i1, not_7_out, not_8_out);
  not not_8 (not_8_out, d0);
  not not_9 (not_9_out, i1);
  not not_10 (not_10_out, i0);
  not not_11 (not_11_out, d1);
  not not_12 (not_12_out, i1);
  not not_13 (not_13_out, d0);
  not not_14 (not_14_out, i0);
  not not_15 (not_15_out, d0);
  not not_16 (not_16_out, d1);
  or or_1 (n1, and_1_out, and_2_out, and_3_out, and_4_out);
  and and_5 (and_5_out, not_9_out, not_10_out, not_11_out, d0);
  and and_6 (and_6_out, not_12_out, i0, not_13_out);
  and and_7 (and_7_out, i1, not_14_out, not_15_out);
  and and_8 (and_8_out, i1, i0, not_16_out, d0);
  or or_2 (n0, and_5_out, and_6_out, and_7_out, and_8_out);
endmodule

module fsm__output_logic (
  input  i1,
  input  i0,
  input  d1,
  input  d0,
  output z
);

  wire not_1_out;

  not not_1 (not_1_out, d0);
  and and_1 (z, i1, i0, not_1_out);
endmodule

module fsm (
  input  [1:0] In,
  input  CLR,
  output Z
);

  wire and_1_out, and_2_out, clock_1_out, fsm_next_state_logic_1_n0, fsm_next_state_logic_1_n1, not_1_out,
       register_1_q, register_2_q;

  Clock clock_1 (.out(clock_1_out));
  not not_1 (not_1_out, CLR);
  fsm__next_state_logic fsm_next_state_logic_1 (
    .i1(register_1_q), .i0(register_2_q), .d1(In[1]), .d0(In[0]), .n1(fsm_next_state_logic_1_n1),
    .n0(fsm_next_state_logic_1_n0));
  and and_1 (and_1_out, not_1_out, fsm_next_state_logic_1_n1);
  Register #(.width(1)) register_1 (.D(and_1_out), .Q(register_1_q), .clk(clock_1_out));  // open: en, clr
  and and_2 (and_2_out, fsm_next_state_logic_1_n0, not_1_out);
  Register #(.width(1)) register_2 (.D(and_2_out), .Q(register_2_q), .clk(clock_1_out));  // open: en, clr
  fsm__output_logic fsm_output_logic_1 (.i1(register_1_q), .i0(register_2_q), .d1(In[1]), .d0(In[0]), .z(Z));
endmodule
