// Logisim project CPU.circ as structural Verilog
module main (
  input  reset,
  output [31:0] pc_w,
  output [31:0] pc_m,
  output regwrite,
  output [4:0] regaddr,
  output [31:0] regdata,
  output memwrite,
  output [31:0] memaddr,
  output [31:0] memdata
);

  wire clk, not_1_out, not_2_out, or_1_out, pause;
  wire [1:0] id_1_ctrl_npc_select;
  wire [4:0] id_1_rs_addr, id_1_rt_addr;
  wire [25:0] id_1_instr_index;
  wire [31:0] exe_1_alu_output, forwardor_1_forwarded, forwardor_2_forwarded, forwardor_3_forwarded,
       forwardor_4_forwarded, grf_1_out_8, grf_1_out_9, id_1_id_result, id_1_immediate, if_1_instruction,
       if_1_pc, mem_1_mem_output, npc_1_npc, npc_1_pc4, rdecoder_1_rd, rsdecoder_1_rs, rtdecoder_1_rt,
       state_register_1_instruction_2, state_register_1_pc4_2, state_register_1_pc_2,
       state_register_2_immediate_2, state_register_2_instruction_2, state_register_2_pc4_2,
       state_register_2_pc_2, state_register_2_rd_addr_2, state_register_2_result_2,
       state_register_2_rs_addr_2, state_register_2_rs_value_2, state_register_2_rt_addr_2,
       state_register_2_rt_value_2, state_register_2_tnew_2, state_register_3_immediate_2,
       state_register_3_instruction_2, state_register_3_pc4_2, state_register_3_rd_addr_2,
       state_register_3_rs_addr_2, state_register_3_rs_value_2, state_register_3_rt_addr_2,
       state_register_3_rt_value_2, state_register_3_tnew_2, state_register_4_instruction_2,
       state_register_4_rd_addr_2, state_register_4_tnew_2, sub1_1_out_2, sub1_2_out_2,
       tnew_decoder_1_rs_tuse;

  not not_1 (not_1_out, pause);
  or or_1 (or_1_out, pause, reset);
  Clock clock_1 (.out(clk));
  not not_2 (not_2_out, pause);
  // Probe on if_1_pc
  IF if_1 (.NPC(npc_1_npc), .PC(if_1_pc), .Instruction(if_1_instruction), .clk(clk), .reset(reset), .enable(not_2_out));
  NPC npc_1 (
    .PC(if_1_pc), .offset(id_1_immediate), .instr_index(id_1_instr_index), .address(forwardor_1_forwarded),
    .PC4(npc_1_pc4), .NPC(npc_1_npc), .ctrl_NPC_select(id_1_ctrl_npc_select));
  state_register state_register_1 (
    .PC(if_1_pc), .PC4(npc_1_pc4), .instruction(if_1_instruction), .PC_2(state_register_1_pc_2),
    .PC4_2(state_register_1_pc4_2), .instruction_2(state_register_1_instruction_2), .enable(not_1_out),
    .clk(clk), .reset(reset));  // open: rs_value, rt_value, immediate, result, rs_addr, rt_addr, rd_addr, tnew, preserved0, preserved1, preserved2, preserved3, preserved4, rs_value_2, rt_value_2, immediate_2, result_2, rs_addr_2, rt_addr_2, rd_addr_2, tnew_2, preserved0_2, preserved1_2, preserved2_2, preserved3_2, preserved4_2
  RSDecoder rsdecoder_1 (.instruction(state_register_1_instruction_2), .rs(rsdecoder_1_rs));
  RTDecoder rtdecoder_1 (.instruction(state_register_1_instruction_2), .rt(rtdecoder_1_rt));
  tnew_decoder tnew_decoder_1 (.instruction(state_register_1_instruction_2), .rs_tuse(tnew_decoder_1_rs_tuse));
  RDecoder rdecoder_1 (.instruction(state_register_1_instruction_2), .rd(rdecoder_1_rd));
  ID id_1 (
    .instruction(state_register_1_instruction_2), .rs(forwardor_1_forwarded), .rt(forwardor_2_forwarded),
    .PC4(state_register_1_pc4_2), .rs_addr(id_1_rs_addr), .rt_addr(id_1_rt_addr),
    .instr_index(id_1_instr_index), .ctrl_NPC_select(id_1_ctrl_npc_select), .immediate(id_1_immediate),
    .ID_result(id_1_id_result));
  pauser pauser_1 (
    .tnew1(state_register_2_tnew_2), .waddr1(state_register_2_rd_addr_2),
    .instruction(state_register_1_instruction_2), .tnew2(state_register_3_tnew_2),
    .waddr2(state_register_3_rd_addr_2), .pause(pause));
  forwardor forwardor_1 (
    .address(rsdecoder_1_rs), .forwarded(forwardor_1_forwarded), .priority0_value(state_register_2_result_2),
    .priority0_tnew(state_register_2_tnew_2), .priority0_address(state_register_2_rd_addr_2),
    .priority1_value(memaddr), .priority1_tnew(state_register_3_tnew_2),
    .priority1_address(state_register_3_rd_addr_2), .fallback(grf_1_out_8));  // open: priority2_value, priority2_tnew, priority2_address
  forwardor forwardor_2 (
    .address(rtdecoder_1_rt), .forwarded(forwardor_2_forwarded), .priority0_value(state_register_2_result_2),
    .priority0_tnew(state_register_2_tnew_2), .priority0_address(state_register_2_rd_addr_2),
    .priority1_value(memaddr), .priority1_tnew(state_register_3_tnew_2),
    .priority1_address(state_register_3_rd_addr_2), .fallback(grf_1_out_9));  // open: priority2_value, priority2_tnew, priority2_address
  state_register state_register_2 (
    .PC(state_register_1_pc_2), .PC4(state_register_1_pc4_2), .instruction(state_register_1_instruction_2),
    .rs_value(forwardor_1_forwarded), .rt_value(forwardor_2_forwarded), .immediate(id_1_immediate),
    .result(id_1_id_result), .rs_addr(rsdecoder_1_rs), .rt_addr(rtdecoder_1_rt), .rd_addr(rdecoder_1_rd),
    .tnew(tnew_decoder_1_rs_tuse), .PC_2(state_register_2_pc_2), .PC4_2(state_register_2_pc4_2),
    .instruction_2(state_register_2_instruction_2), .rs_value_2(state_register_2_rs_value_2),
    .rt_value_2(state_register_2_rt_value_2), .immediate_2(state_register_2_immediate_2),
    .result_2(state_register_2_result_2), .rs_addr_2(state_register_2_rs_addr_2),
    .rt_addr_2(state_register_2_rt_addr_2), .rd_addr_2(state_register_2_rd_addr_2),
    .tnew_2(state_register_2_tnew_2), .clk(clk), .reset(or_1_out));  // open: preserved0, preserved1, preserved2, preserved3, preserved4, preserved0_2, preserved1_2, preserved2_2, preserved3_2, preserved4_2, enable
  GRF grf_1 (
    .Input(regdata), .read_addr0(id_1_rs_addr), .read_addr1(id_1_rt_addr), .write_enable(regwrite),
    .write_addr(regaddr), .out_8(grf_1_out_8), .out_9(grf_1_out_9), .Clock(clk), .Reset(reset));
  sub1 sub1_1 (.in_1(state_register_2_tnew_2), .out_2(sub1_1_out_2));
  EXE exe_1 (
    .rs(forwardor_3_forwarded), .rt(forwardor_4_forwarded), .immediate(state_register_2_immediate_2),
    .ALU_output(exe_1_alu_output), .ID_result(state_register_2_result_2),
    .instruction(state_register_2_instruction_2));
  forwardor forwardor_3 (
    .address(state_register_2_rs_addr_2), .forwarded(forwardor_3_forwarded), .priority0_value(memaddr),
    .priority0_tnew(state_register_3_tnew_2), .priority0_address(state_register_3_rd_addr_2),
    .priority1_value(regdata), .priority1_tnew(state_register_4_tnew_2),
    .priority1_address(state_register_4_rd_addr_2), .fallback(state_register_2_rs_value_2));  // open: priority2_value, priority2_tnew, priority2_address
  forwardor forwardor_4 (
    .address(state_register_2_rt_addr_2), .forwarded(forwardor_4_forwarded), .priority0_value(memaddr),
    .priority0_tnew(state_register_3_tnew_2), .priority0_address(state_register_3_rd_addr_2),
    .priority1_value(regdata), .priority1_tnew(state_register_4_tnew_2),
    .priority1_address(state_register_4_rd_addr_2), .fallback(state_register_2_rt_value_2));  // open: priority2_value, priority2_tnew, priority2_address
  state_register state_register_3 (
    .PC(state_register_2_pc_2), .PC4(state_register_2_pc4_2), .instruction(state_register_2_instruction_2),
    .rs_value(forwardor_3_forwarded), .rt_value(forwardor_4_forwarded),
    .immediate(state_register_2_immediate_2), .result(exe_1_alu_output),
    .rs_addr(state_register_2_rs_addr_2), .rt_addr(state_register_2_rt_addr_2),
    .rd_addr(state_register_2_rd_addr_2), .tnew(sub1_1_out_2), .PC_2(pc_m), .PC4_2(state_register_3_pc4_2),
    .instruction_2(state_register_3_instruction_2), .rs_value_2(state_register_3_rs_value_2),
    .rt_value_2(state_register_3_rt_value_2), .immediate_2(state_register_3_immediate_2), .result_2(memaddr),
    .rs_addr_2(state_register_3_rs_addr_2), .rt_addr_2(state_register_3_rt_addr_2),
    .rd_addr_2(state_register_3_rd_addr_2), .tnew_2(state_register_3_tnew_2), .clk(clk), .reset(reset));  // open: preserved0, preserved1, preserved2, preserved3, preserved4, preserved0_2, preserved1_2, preserved2_2, preserved3_2, preserved4_2, enable
  sub1 sub1_2 (.in_1(state_register_3_tnew_2), .out_2(sub1_2_out_2));
  MEM mem_1 (
    .EXE_output(memaddr), .rt(memdata), .clk(clk), .reset(reset),
    .instruction(state_register_3_instruction_2), .MEM_output(mem_1_mem_output), .out_7(memwrite));
  forwardor forwardor_5 (
    .address(state_register_3_rs_addr_2), .priority0_value(regdata),
    .priority0_tnew(state_register_4_tnew_2), .priority0_address(state_register_4_rd_addr_2));  // open: forwarded, priority1_value, priority1_tnew, priority1_address, priority2_value, priority2_tnew, priority2_address, fallback
  forwardor forwardor_6 (
    .address(state_register_3_rt_addr_2), .forwarded(memdata), .priority0_value(regdata),
    .priority0_tnew(state_register_4_tnew_2), .priority0_address(state_register_4_rd_addr_2),
    .fallback(state_register_3_rt_value_2));  // open: priority1_value, priority1_tnew, priority1_address, priority2_value, priority2_tnew, priority2_address
  state_register state_register_4 (
    .PC(pc_m), .PC4(state_register_3_pc4_2), .instruction(state_register_3_instruction_2),
    .rs_value(state_register_3_rs_value_2), .rt_value(memdata), .immediate(state_register_3_immediate_2),
    .result(mem_1_mem_output), .rs_addr(state_register_3_rs_addr_2), .rt_addr(state_register_3_rt_addr_2),
    .rd_addr(state_register_3_rd_addr_2), .tnew(sub1_2_out_2), .PC_2(pc_w),
    .instruction_2(state_register_4_instruction_2), .result_2(regdata),
    .rd_addr_2(state_register_4_rd_addr_2), .tnew_2(state_register_4_tnew_2), .clk(clk), .reset(reset));  // open: preserved0, preserved1, preserved2, preserved3, preserved4, PC4_2, rs_value_2, rt_value_2, immediate_2, rs_addr_2, rt_addr_2, preserved0_2, preserved1_2, preserved2_2, preserved3_2, preserved4_2, enable
  WB wb_1 (.instruction(state_register_4_instruction_2), .ctrl_GRF_write(regwrite), .GRF_write_address(regaddr));
  // Probe on pc_w

  // Other names for the same wires on the sheet: mema[31:0] = memaddr; memd[31:0] = memdata; memw = memwrite;
  //   rega[4:0] = regaddr; regd[31:0] = regdata; regw = regwrite
endmodule

module IF (
  input  [31:0] NPC,
  input  enable,
  input  clk,
  input  reset,
  output [31:0] PC,
  output [31:0] Instruction
);

  _32bit_register u_PC (.D(NPC), .Initial_Value(32'h3000), .enable(enable), .Q(PC), .clk(clk), .reset(reset));
  ROM #(.addrWidth(10), .dataWidth(32)) rom_1 (.addr(PC[11:2]), .data(Instruction));  // open: sel

  // Notes on the sheet:
  //   contents of rom_1 (hex, n*v repeats v):
  //   5*34011010
endmodule

module ID (
  input  [31:0] instruction,
  input  [31:0] rs,
  input  [31:0] rt,
  input  [31:0] PC4,
  output [4:0] rs_addr,
  output [4:0] rt_addr,
  output [25:0] instr_index,
  output [1:0] ctrl_NPC_select,
  output [31:0] immediate,
  output [31:0] ID_result
);

  wire cp_result, ctrl_ID_result_select, ctrl_immediate_select, ctrl_signed_extend;
  wire [1:0] proposal_NPC_select;
  wire [2:0] ctrl_comparator_select;
  wire [31:0] B_offset, extend_immediate, PC8;

  _16_32bit_extender u_16_32bit_extender_1 (
    .origin(instruction[15:0]), .ctrl_signed_extend(ctrl_signed_extend), .result(extend_immediate));
  B_extender b_extender_1 (.immediate(instruction[15:0]), .offset(B_offset));
  _32bit_adder u_32bit_adder_1 (.A(PC4), .B(32'h4), .S(PC8));  // open: cin, cout
  _32bit_selective_comparator u_32bit_selective_comparator_1 (
    .A(rs), .B(rt), .comparator_result(cp_result), .ctrl_comparator_select(ctrl_comparator_select));
  assign ctrl_NPC_select = proposal_NPC_select & {2{cp_result}};  // AND_Gate and_1, 2 bits wide
  Multiplexer #(.width(32), .enable("false")) multiplexer_1 (
    .in0(extend_immediate), .in1(B_offset), .out(immediate), .sel(ctrl_immediate_select));
  Multiplexer #(.width(32), .enable("false")) multiplexer_2 (
    .in0({instruction[15:0], {16{1'b0}}}), .in1(PC8), .out(ID_result), .sel(ctrl_ID_result_select));
  ctrl_ID ctrl_id_1 (
    .opcode(instruction[31:26]), .funct(instruction[5:0]), .ctrl_NPC_select(proposal_NPC_select),
    .ctrl_ID_result_select(ctrl_ID_result_select), .ctrl_signed_extend(ctrl_signed_extend),
    .ctrl_immediate_select(ctrl_immediate_select), .ctrl_comparator_select(ctrl_comparator_select));

  assign instr_index = instruction[25:0];
  assign rs_addr = instruction[25:21];
  assign rt_addr = instruction[20:16];

  // Other names for the same wires on the sheet: origin_immediate[15:0] = instruction[15:0];
  //   sll16[31:16] = instruction[15:0]

  // Notes on the sheet:
  //   rs
  //   rt
  //   immediate
  //   instr_index
  //   opcode
  //   funct
endmodule

module NPC (
  input  [1:0] ctrl_NPC_select,
  input  [31:0] PC,
  input  [31:0] offset,
  input  [25:0] instr_index,
  input  [31:0] address,
  output [31:0] PC4,
  output [31:0] NPC
);

  wire [31:0] n32bit_adder_2_s;

  _32bit_adder u_32bit_adder_1 (.A(PC), .B(32'h4), .S(PC4));  // open: cin, cout
  _32bit_adder u_32bit_adder_2 (.A(PC), .B(offset), .S(n32bit_adder_2_s));  // open: cin, cout
  Multiplexer #(.select(2), .width(32), .disabled(0), .enable("false")) multiplexer_1 (
    .in0(PC4), .in1(n32bit_adder_2_s), .in2({PC[31:28], instr_index, 2'b00}), .in3(address), .out(NPC),
    .sel(ctrl_NPC_select));
endmodule

module GRF (
  input  [31:0] Input,
  input  [4:0] read_addr0,
  input  [4:0] read_addr1,
  input  write_enable,
  input  [4:0] write_addr,
  input  Clock,
  input  Reset,
  output [31:0] out_8,
  output [31:0] out_9
);

  wire decoder_1_out0, decoder_1_out1, decoder_1_out2, decoder_1_out3, decoder_1_out4, decoder_1_out5,
       decoder_1_out6, decoder_1_out7, decoder_1_out8, decoder_1_out9, decoder_1_out10, decoder_1_out11,
       decoder_1_out12, decoder_1_out13, decoder_1_out14, decoder_1_out15, decoder_1_out16, decoder_1_out17,
       decoder_1_out18, decoder_1_out19, decoder_1_out20, decoder_1_out21, decoder_1_out22, decoder_1_out23,
       decoder_1_out24, decoder_1_out25, decoder_1_out26, decoder_1_out27, decoder_1_out28, decoder_1_out29,
       decoder_1_out30, decoder_1_out31;
  wire [31:0] a0_4_q, a1_5_q, a2_6_q, a3_7_q, at_1_q, fp_30_q, gp_28_q, k0_26_q, k1_27_q, ra_31_q, s0_16_q,
       s1_17_q, s2_18_q, s3_19_q, s4_20_q, s5_21_q, s6_22_q, s7_23_q, sp_29_q, t0_8_q, t1_9_q, t2_10_q,
       t3_11_q, t4_12_q, t5_13_q, t6_14_q, t7_15_q, t8_24_q, t9_25_q, v0_2_q, v1_3_q, zero_0_q;

  Decoder #(.select(5), .disabled(0)) decoder_1 (
    .out0(decoder_1_out0), .out1(decoder_1_out1), .out2(decoder_1_out2), .out3(decoder_1_out3),
    .out4(decoder_1_out4), .out5(decoder_1_out5), .out6(decoder_1_out6), .out7(decoder_1_out7),
    .out8(decoder_1_out8), .out9(decoder_1_out9), .out10(decoder_1_out10), .out11(decoder_1_out11),
    .out12(decoder_1_out12), .out13(decoder_1_out13), .out14(decoder_1_out14), .out15(decoder_1_out15),
    .out16(decoder_1_out16), .out17(decoder_1_out17), .out18(decoder_1_out18), .out19(decoder_1_out19),
    .out20(decoder_1_out20), .out21(decoder_1_out21), .out22(decoder_1_out22), .out23(decoder_1_out23),
    .out24(decoder_1_out24), .out25(decoder_1_out25), .out26(decoder_1_out26), .out27(decoder_1_out27),
    .out28(decoder_1_out28), .out29(decoder_1_out29), .out30(decoder_1_out30), .out31(decoder_1_out31),
    .sel(write_addr), .en(write_enable));
  _32bit_write_through_register zero_0 (
    .en(decoder_1_out0), .Q(zero_0_q), .clk(Clock), .reset(Reset));  // open: D, Init
  _32bit_write_through_register at_1 (
    .D(Input), .en(decoder_1_out1), .Q(at_1_q), .clk(Clock), .reset(Reset));  // open: Init
  _32bit_write_through_register v0_2 (
    .D(Input), .en(decoder_1_out2), .Q(v0_2_q), .clk(Clock), .reset(Reset));  // open: Init
  _32bit_write_through_register v1_3 (
    .D(Input), .en(decoder_1_out3), .Q(v1_3_q), .clk(Clock), .reset(Reset));  // open: Init
  _32bit_write_through_register a0_4 (
    .D(Input), .en(decoder_1_out4), .Q(a0_4_q), .clk(Clock), .reset(Reset));  // open: Init
  _32bit_write_through_register a1_5 (
    .D(Input), .en(decoder_1_out5), .Q(a1_5_q), .clk(Clock), .reset(Reset));  // open: Init
  _32bit_write_through_register a2_6 (
    .D(Input), .en(decoder_1_out6), .Q(a2_6_q), .clk(Clock), .reset(Reset));  // open: Init
  _32bit_write_through_register a3_7 (
    .D(Input), .en(decoder_1_out7), .Q(a3_7_q), .clk(Clock), .reset(Reset));  // open: Init
  _32bit_write_through_register t0_8 (
    .D(Input), .en(decoder_1_out8), .Q(t0_8_q), .clk(Clock), .reset(Reset));  // open: Init
  _32bit_write_through_register t1_9 (
    .D(Input), .en(decoder_1_out9), .Q(t1_9_q), .clk(Clock), .reset(Reset));  // open: Init
  _32bit_write_through_register t2_10 (
    .D(Input), .en(decoder_1_out10), .Q(t2_10_q), .clk(Clock), .reset(Reset));  // open: Init
  _32bit_write_through_register t3_11 (
    .D(Input), .en(decoder_1_out11), .Q(t3_11_q), .clk(Clock), .reset(Reset));  // open: Init
  _32bit_write_through_register t4_12 (
    .D(Input), .en(decoder_1_out12), .Q(t4_12_q), .clk(Clock), .reset(Reset));  // open: Init
  _32bit_write_through_register t5_13 (
    .D(Input), .en(decoder_1_out13), .Q(t5_13_q), .clk(Clock), .reset(Reset));  // open: Init
  _32bit_write_through_register t6_14 (
    .D(Input), .en(decoder_1_out14), .Q(t6_14_q), .clk(Clock), .reset(Reset));  // open: Init
  _32bit_write_through_register t7_15 (
    .D(Input), .en(decoder_1_out15), .Q(t7_15_q), .clk(Clock), .reset(Reset));  // open: Init
  _32bit_write_through_register s0_16 (
    .D(Input), .en(decoder_1_out16), .Q(s0_16_q), .clk(Clock), .reset(Reset));  // open: Init
  _32bit_write_through_register s1_17 (
    .D(Input), .en(decoder_1_out17), .Q(s1_17_q), .clk(Clock), .reset(Reset));  // open: Init
  _32bit_write_through_register s2_18 (
    .D(Input), .en(decoder_1_out18), .Q(s2_18_q), .clk(Clock), .reset(Reset));  // open: Init
  _32bit_write_through_register s3_19 (
    .D(Input), .en(decoder_1_out19), .Q(s3_19_q), .clk(Clock), .reset(Reset));  // open: Init
  _32bit_write_through_register s4_20 (
    .D(Input), .en(decoder_1_out20), .Q(s4_20_q), .clk(Clock), .reset(Reset));  // open: Init
  _32bit_write_through_register s5_21 (
    .D(Input), .en(decoder_1_out21), .Q(s5_21_q), .clk(Clock), .reset(Reset));  // open: Init
  _32bit_write_through_register s6_22 (
    .D(Input), .en(decoder_1_out22), .Q(s6_22_q), .clk(Clock), .reset(Reset));  // open: Init
  _32bit_write_through_register s7_23 (
    .D(Input), .en(decoder_1_out23), .Q(s7_23_q), .clk(Clock), .reset(Reset));  // open: Init
  _32bit_write_through_register t8_24 (
    .D(Input), .en(decoder_1_out24), .Q(t8_24_q), .clk(Clock), .reset(Reset));  // open: Init
  _32bit_write_through_register t9_25 (
    .D(Input), .en(decoder_1_out25), .Q(t9_25_q), .clk(Clock), .reset(Reset));  // open: Init
  _32bit_write_through_register k0_26 (
    .D(Input), .en(decoder_1_out26), .Q(k0_26_q), .clk(Clock), .reset(Reset));  // open: Init
  _32bit_write_through_register k1_27 (
    .D(Input), .en(decoder_1_out27), .Q(k1_27_q), .clk(Clock), .reset(Reset));  // open: Init
  _32bit_write_through_register gp_28 (
    .D(Input), .en(decoder_1_out28), .Q(gp_28_q), .clk(Clock), .reset(Reset));  // open: Init
  _32bit_write_through_register sp_29 (
    .D(Input), .Init(32'h2ffc), .en(decoder_1_out29), .Q(sp_29_q), .clk(Clock), .reset(Reset));
  _32bit_write_through_register fp_30 (
    .D(Input), .en(decoder_1_out30), .Q(fp_30_q), .clk(Clock), .reset(Reset));  // open: Init
  _32bit_write_through_register ra_31 (
    .D(Input), .en(decoder_1_out31), .Q(ra_31_q), .clk(Clock), .reset(Reset));  // open: Init
  Multiplexer #(.select(5), .width(32), .enable("false")) multiplexer_1 (
    .in0(zero_0_q), .in1(at_1_q), .in2(v0_2_q), .in3(v1_3_q), .in4(a0_4_q), .in5(a1_5_q), .in6(a2_6_q),
    .in7(a3_7_q), .in8(t0_8_q), .in9(t1_9_q), .in10(t2_10_q), .in11(t3_11_q), .in12(t4_12_q), .in13(t5_13_q),
    .in14(t6_14_q), .in15(t7_15_q), .in16(s0_16_q), .in17(s1_17_q), .in18(s2_18_q), .in19(s3_19_q),
    .in20(s4_20_q), .in21(s5_21_q), .in22(s6_22_q), .in23(s7_23_q), .in24(t8_24_q), .in25(t9_25_q),
    .in26(k0_26_q), .in27(k1_27_q), .in28(gp_28_q), .in29(sp_29_q), .in30(fp_30_q), .in31(ra_31_q),
    .out(out_8), .sel(read_addr0));
  Multiplexer #(.select(5), .width(32), .enable("false")) multiplexer_2 (
    .in0(zero_0_q), .in1(at_1_q), .in2(v0_2_q), .in3(v1_3_q), .in4(a0_4_q), .in5(a1_5_q), .in6(a2_6_q),
    .in7(a3_7_q), .in8(t0_8_q), .in9(t1_9_q), .in10(t2_10_q), .in11(t3_11_q), .in12(t4_12_q), .in13(t5_13_q),
    .in14(t6_14_q), .in15(t7_15_q), .in16(s0_16_q), .in17(s1_17_q), .in18(s2_18_q), .in19(s3_19_q),
    .in20(s4_20_q), .in21(s5_21_q), .in22(s6_22_q), .in23(s7_23_q), .in24(t8_24_q), .in25(t9_25_q),
    .in26(k0_26_q), .in27(k1_27_q), .in28(gp_28_q), .in29(sp_29_q), .in30(fp_30_q), .in31(ra_31_q),
    .out(out_9), .sel(read_addr1));

  // Notes on the sheet:
  //   write_enable: pull=down
  //   Reset: pull=down
endmodule

module _32bit_adder (
  input  [31:0] A,
  input  cin,
  input  [31:0] B,
  output [31:0] S,
  output cout
);

  Adder #(.width(32)) adder_1 (.a(A), .b(B), .out(S), .cin(cin), .cout(cout));

  // Notes on the sheet:
  //   cin: pull=down
endmodule

module _32bit_a_s (
  input  sub,
  input  [31:0] A,
  input  [31:0] B,
  output [31:0] S
);

  wire [31:0] multiplexer_1_out, not_1_out;

  Multiplexer #(.width(32), .disabled(0), .enable("false")) multiplexer_1 (
    .in0(B), .in1(not_1_out), .out(multiplexer_1_out), .sel(sub));
  assign not_1_out = ~B;  // NOT_Gate not_1, 32 bits wide
  _32bit_adder u_32bit_adder_1 (.A(A), .B(multiplexer_1_out), .S(S), .cin(sub));  // open: cout
endmodule

module _32bit_register (
  input  [31:0] D,
  input  [31:0] Initial_Value,
  input  enable,
  input  clk,
  input  reset,
  output [31:0] Q
);

  wire [31:0] n32bit_adder_1_s, negator_1_out, register_1_q;

  Negator #(.width(32)) negator_1 (.in(Initial_Value), .out(negator_1_out));
  _32bit_adder u_32bit_adder_1 (.A(D), .B(negator_1_out), .S(n32bit_adder_1_s));  // open: cin, cout
  Register #(.width(32)) register_1 (.D(n32bit_adder_1_s), .en(enable), .Q(register_1_q), .clk(clk), .clr(reset));
  _32bit_adder u_32bit_adder_2 (.A(register_1_q), .B(Initial_Value), .S(Q));  // open: cin, cout

  // Notes on the sheet:
  //   enable: pull=up
  //   Initial_Value: pull=down
endmodule

module _32bit_write_through_register (
  input  [31:0] D,
  input  [31:0] Init,
  input  en,
  input  clk,
  input  reset,
  output [31:0] Q
);

  wire [31:0] n32bit_register_1_q;

  _32bit_register u_32bit_register_1 (
    .D(D), .Initial_Value(Init), .enable(en), .Q(n32bit_register_1_q), .clk(clk), .reset(reset));
  Multiplexer #(.width(32), .disabled(0), .enable("false")) multiplexer_1 (
    .in0(n32bit_register_1_q), .in1(D), .out(Q), .sel(en));

  // Notes on the sheet:
  //   D: pull=down
  //   Init: pull=down
endmodule

module instruction_splitter (
  input  [31:0] Instruction,
  output [25:0] address,
  output [15:0] offset,
  output [5:0] funct,
  output [4:0] shamt,
  output [4:0] rd,
  output [4:0] rt,
  output [4:0] rs,
  output [5:0] opcode
);


  assign address = Instruction[25:0];
  assign funct = Instruction[5:0];
  assign offset = Instruction[15:0];
  assign opcode = Instruction[31:26];
  assign rd = Instruction[15:11];
  assign rs = Instruction[25:21];
  assign rt = Instruction[20:16];
  assign shamt = Instruction[10:6];
endmodule

module B_extender (
  input  [15:0] immediate,
  output [31:0] offset
);


  assign offset = {{15{immediate[15]}}, immediate[14:0], 2'b00};
endmodule

module _16_32bit_extender (
  input  [15:0] origin,
  input  ctrl_signed_extend,
  output [31:0] result
);

  and and_1 (result[31], origin[15], ctrl_signed_extend);

  assign result[30:0] = {{15{result[31]}}, origin};
endmodule

module _32bit_comparator (
  input  [31:0] A,
  input  [31:0] B,
  output gt,
  output eq,
  output lt
);

  Comparator #(.width(32)) comparator_1 (.a(A), .b(B), .gt(gt), .eq(eq), .lt(lt));
endmodule

module _32bit_extend_comparator (
  input  [31:0] A,
  input  [31:0] B,
  output _1,
  output ge,
  output gt,
  output eq,
  output ne,
  output lt,
  output le,
  output _0
);

  _32bit_comparator u_32bit_comparator_1 (.A(A), .B(B), .gt(gt), .eq(eq), .lt(lt));
  or or_1 (ge, gt, eq);
  or or_2 (le, eq, lt);
  or or_3 (ne, gt, lt);

  assign _0 = 1'b0;
  assign _1 = 1'b1;
endmodule

module _32bit_selective_comparator (
  input  [2:0] ctrl_comparator_select,
  input  [31:0] A,
  input  [31:0] B,
  output comparator_result
);

  wire n32bit_extend_comparator_1__0, n32bit_extend_comparator_1__1, n32bit_extend_comparator_1_eq,
       n32bit_extend_comparator_1_ge, n32bit_extend_comparator_1_gt, n32bit_extend_comparator_1_le,
       n32bit_extend_comparator_1_lt, n32bit_extend_comparator_1_ne;

  _32bit_extend_comparator u_32bit_extend_comparator_1 (
    .A(A), .B(B), ._1(n32bit_extend_comparator_1__1), .ge(n32bit_extend_comparator_1_ge),
    .gt(n32bit_extend_comparator_1_gt), .eq(n32bit_extend_comparator_1_eq),
    .ne(n32bit_extend_comparator_1_ne), .lt(n32bit_extend_comparator_1_lt),
    .le(n32bit_extend_comparator_1_le), ._0(n32bit_extend_comparator_1__0));
  Multiplexer #(.select(3), .enable("false")) multiplexer_1 (
    .in0(n32bit_extend_comparator_1__1), .in1(n32bit_extend_comparator_1_ge),
    .in2(n32bit_extend_comparator_1_gt), .in3(n32bit_extend_comparator_1_eq),
    .in4(n32bit_extend_comparator_1_ne), .in5(n32bit_extend_comparator_1_lt),
    .in6(n32bit_extend_comparator_1_le), .in7(n32bit_extend_comparator_1__0), .out(comparator_result),
    .sel(ctrl_comparator_select));
endmodule

module EXE (
  input  [31:0] instruction,
  input  [31:0] rs,
  input  [31:0] rt,
  input  [31:0] immediate,
  input  [31:0] ID_result,
  output [31:0] ALU_output
);

  wire ctrl_ALU_operand2_select, ctrl_ALU_sub;
  wire [1:0] ctrl_ALU_output_select;
  wire [31:0] a_s_result, operand2, or_result;

  Multiplexer #(.width(32), .disabled(0), .enable("false")) multiplexer_1 (
    .in0(rt), .in1(immediate), .out(operand2), .sel(ctrl_ALU_operand2_select));
  ctrl_EXE ctrl_exe_1 (
    .opcode(instruction[31:26]), .funct(instruction[5:0]), .ctrl_ALU_sub(ctrl_ALU_sub),
    .ctrl_ALU_operand2_select(ctrl_ALU_operand2_select), .ctrl_ALU_output_select(ctrl_ALU_output_select));
  _32bit_a_s u_32bit_a_s_1 (.A(rs), .B(operand2), .S(a_s_result), .sub(ctrl_ALU_sub));
  assign or_result = rs | operand2;  // OR_Gate or_1, 32 bits wide
  Multiplexer #(.select(2), .width(32), .disabled(0), .enable("false")) multiplexer_2 (
    .in0(a_s_result), .in1(or_result), .in2(ID_result), .out(ALU_output), .sel(ctrl_ALU_output_select));  // open: in3

  // Other names for the same wires on the sheet: operand1[31:0] = rs

  // Notes on the sheet:
  //   opcode
  //   funct
endmodule

module templates (
);


  // Notes on the sheet:
  //   opcode
  //   rs
  //   rt
  //   rd
  //   shamt
  //   funct
  //   instr_index
  //   immediate
endmodule

module ctrl_ID (
  input  [5:0] opcode,
  input  [5:0] funct,
  output [1:0] ctrl_NPC_select,
  output ctrl_ID_result_select,
  output ctrl_signed_extend,
  output ctrl_immediate_select,
  output [2:0] ctrl_comparator_select
);

  wire instruction_decoder_1_addu, instruction_decoder_1_beq, instruction_decoder_1_j,
       instruction_decoder_1_jal, instruction_decoder_1_jr, instruction_decoder_1_lui,
       instruction_decoder_1_lw, instruction_decoder_1_ori, instruction_decoder_1_subu,
       instruction_decoder_1_sw;

  instruction_decoder instruction_decoder_1 (
    .opcode(opcode), .funct(funct), .addu(instruction_decoder_1_addu), .subu(instruction_decoder_1_subu),
    .ori(instruction_decoder_1_ori), .lui(instruction_decoder_1_lui), .lw(instruction_decoder_1_lw),
    .sw(instruction_decoder_1_sw), .beq(instruction_decoder_1_beq), .j(instruction_decoder_1_j),
    .jal(instruction_decoder_1_jal), .jr(instruction_decoder_1_jr));
  or or_1 (ctrl_NPC_select[0], instruction_decoder_1_beq, instruction_decoder_1_jr);
  or or_2 (ctrl_NPC_select[1], instruction_decoder_1_j, instruction_decoder_1_jr, instruction_decoder_1_jal);
  buf or_3 (ctrl_ID_result_select, instruction_decoder_1_jal);  // OR_Gate
  or or_4 (ctrl_signed_extend, instruction_decoder_1_lw, instruction_decoder_1_sw);
  buf or_5 (ctrl_immediate_select, instruction_decoder_1_beq);  // OR_Gate
  buf or_6 (ctrl_comparator_select[0], instruction_decoder_1_beq);  // OR_Gate
  buf or_7 (ctrl_comparator_select[1], instruction_decoder_1_beq);  // OR_Gate
  // OR_Gate or_8 is placed but not wired

  assign ctrl_comparator_select[2] = 1'b0;
endmodule

module instruction_decoder (
  input  [5:0] opcode,
  input  [5:0] funct,
  output addu,
  output subu,
  output ori,
  output lui,
  output lw,
  output sw,
  output beq,
  output j,
  output jal,
  output jr
);

  wire nor_1_out;

  nor nor_1 (nor_1_out, opcode[0], opcode[1], opcode[2], opcode[3], opcode[4], opcode[5]);
  and and_1 (addu, nor_1_out, funct[0], ~funct[1], ~funct[2], ~funct[3], ~funct[4], funct[5]);  // AND_Gate
  and and_2 (subu, nor_1_out, funct[0], funct[1], ~funct[2], ~funct[3], ~funct[4], funct[5]);  // AND_Gate
  and and_3 (ori, opcode[0], ~opcode[1], opcode[2], opcode[3], ~opcode[4], ~opcode[5]);  // AND_Gate
  and and_4 (lui, opcode[0], opcode[1], opcode[2], opcode[3], ~opcode[4], ~opcode[5]);  // AND_Gate
  and and_5 (lw, opcode[0], opcode[1], ~opcode[2], ~opcode[3], ~opcode[4], opcode[5]);  // AND_Gate
  and and_6 (sw, opcode[0], opcode[1], ~opcode[2], opcode[3], ~opcode[4], opcode[5]);  // AND_Gate
  and and_7 (beq, ~opcode[0], ~opcode[1], opcode[2], ~opcode[3], ~opcode[4], ~opcode[5]);  // AND_Gate
  and and_8 (j, ~opcode[0], opcode[1], ~opcode[2], ~opcode[3], ~opcode[4], ~opcode[5]);  // AND_Gate
  and and_9 (jal, opcode[0], opcode[1], ~opcode[2], ~opcode[3], ~opcode[4], ~opcode[5]);  // AND_Gate
  and and_10 (jr, nor_1_out, ~funct[0], ~funct[1], ~funct[2], funct[3], ~funct[4], ~funct[5]);  // AND_Gate
endmodule

module ctrl_EXE (
  input  [5:0] opcode,
  input  [5:0] funct,
  output ctrl_ALU_sub,
  output ctrl_ALU_operand2_select,
  output [1:0] ctrl_ALU_output_select
);

  wire instruction_decoder_1_addu, instruction_decoder_1_beq, instruction_decoder_1_j,
       instruction_decoder_1_jal, instruction_decoder_1_jr, instruction_decoder_1_lui,
       instruction_decoder_1_lw, instruction_decoder_1_ori, instruction_decoder_1_subu,
       instruction_decoder_1_sw;

  instruction_decoder instruction_decoder_1 (
    .opcode(opcode), .funct(funct), .addu(instruction_decoder_1_addu), .subu(instruction_decoder_1_subu),
    .ori(instruction_decoder_1_ori), .lui(instruction_decoder_1_lui), .lw(instruction_decoder_1_lw),
    .sw(instruction_decoder_1_sw), .beq(instruction_decoder_1_beq), .j(instruction_decoder_1_j),
    .jal(instruction_decoder_1_jal), .jr(instruction_decoder_1_jr));
  buf or_1 (ctrl_ALU_sub, instruction_decoder_1_subu);  // OR_Gate
  or or_2 (ctrl_ALU_operand2_select, instruction_decoder_1_ori, instruction_decoder_1_lw, instruction_decoder_1_sw);
  buf or_3 (ctrl_ALU_output_select[0], instruction_decoder_1_ori);  // OR_Gate
  or or_4 (ctrl_ALU_output_select[1], instruction_decoder_1_jal, instruction_decoder_1_lui);
endmodule

module MEM (
  input  [31:0] EXE_output,
  input  [31:0] rt,
  input  clk,
  input  reset,
  input  [31:0] instruction,
  output [31:0] MEM_output,
  output out_7
);

  wire ctrl_MEM_read, not_1_out;

  not not_1 (not_1_out, ctrl_MEM_read);
  assign MEM_output = not_1_out ? EXE_output : 32'bz;  // Controlled_Buffer controlled_buffer_1
  RAM #(.addrWidth(10), .dataWidth(32), .bus("separate")) ram_1 (
    .addr(EXE_output[11:2]), .din(rt), .data(MEM_output), .str(out_7), .clk(clk), .ld(ctrl_MEM_read),
    .clr(reset));  // open: sel
  ctrl_MEM ctrl_mem_1 (
    .opcode(instruction[31:26]), .funct(instruction[5:0]), .ctrl_MEM_read(ctrl_MEM_read),
    .ctrl_MEM_write(out_7));

  // Other names for the same wires on the sheet: ctrl_MEM_write = out_7

  // Notes on the sheet:
  //   opcode
  //   funct
endmodule

module ctrl_MEM (
  input  [5:0] opcode,
  input  [5:0] funct,
  output ctrl_MEM_read,
  output ctrl_MEM_write
);

  wire instruction_decoder_1_addu, instruction_decoder_1_beq, instruction_decoder_1_j,
       instruction_decoder_1_jal, instruction_decoder_1_jr, instruction_decoder_1_lui,
       instruction_decoder_1_lw, instruction_decoder_1_ori, instruction_decoder_1_subu,
       instruction_decoder_1_sw;

  instruction_decoder instruction_decoder_1 (
    .opcode(opcode), .funct(funct), .addu(instruction_decoder_1_addu), .subu(instruction_decoder_1_subu),
    .ori(instruction_decoder_1_ori), .lui(instruction_decoder_1_lui), .lw(instruction_decoder_1_lw),
    .sw(instruction_decoder_1_sw), .beq(instruction_decoder_1_beq), .j(instruction_decoder_1_j),
    .jal(instruction_decoder_1_jal), .jr(instruction_decoder_1_jr));
  buf or_1 (ctrl_MEM_read, instruction_decoder_1_lw);  // OR_Gate
  buf or_2 (ctrl_MEM_write, instruction_decoder_1_sw);  // OR_Gate
endmodule

module WB (
  input  [31:0] instruction,
  output ctrl_GRF_write,
  output [4:0] GRF_write_address
);

  wire [1:0] ctrl_GRF_write_address_select;

  Multiplexer #(.select(2), .width(5), .enable("false")) multiplexer_1 (
    .in0(instruction[15:11]), .in1(instruction[20:16]), .in2({5{1'b1}}), .out(GRF_write_address),
    .sel(ctrl_GRF_write_address_select));  // open: in3
  ctrl_WB ctrl_wb_1 (
    .opcode(instruction[31:26]), .funct(instruction[5:0]), .ctrl_GRF_write(ctrl_GRF_write),
    .ctrl_GRF_write_address_select(ctrl_GRF_write_address_select));

  // Notes on the sheet:
  //   opcode
  //   funct
  //   rd
  //   rt
endmodule

module ctrl_WB (
  input  [5:0] opcode,
  input  [5:0] funct,
  output ctrl_GRF_write,
  output [1:0] ctrl_GRF_write_address_select
);

  wire instruction_decoder_1_addu, instruction_decoder_1_beq, instruction_decoder_1_j,
       instruction_decoder_1_jal, instruction_decoder_1_jr, instruction_decoder_1_lui,
       instruction_decoder_1_lw, instruction_decoder_1_ori, instruction_decoder_1_subu,
       instruction_decoder_1_sw;

  instruction_decoder instruction_decoder_1 (
    .opcode(opcode), .funct(funct), .addu(instruction_decoder_1_addu), .subu(instruction_decoder_1_subu),
    .ori(instruction_decoder_1_ori), .lui(instruction_decoder_1_lui), .lw(instruction_decoder_1_lw),
    .sw(instruction_decoder_1_sw), .beq(instruction_decoder_1_beq), .j(instruction_decoder_1_j),
    .jal(instruction_decoder_1_jal), .jr(instruction_decoder_1_jr));
  or or_1 (ctrl_GRF_write, instruction_decoder_1_addu, instruction_decoder_1_subu, instruction_decoder_1_ori, instruction_decoder_1_lui, instruction_decoder_1_lw, instruction_decoder_1_jal);
  or or_2 (ctrl_GRF_write_address_select[0], instruction_decoder_1_ori, instruction_decoder_1_lui, instruction_decoder_1_lw);
  buf or_3 (ctrl_GRF_write_address_select[1], instruction_decoder_1_jal);  // OR_Gate
endmodule

module state_register (
  input  [31:0] PC,
  input  [31:0] PC4,
  input  [31:0] instruction,
  input  [31:0] rs_value,
  input  [31:0] rt_value,
  input  [31:0] immediate,
  input  [31:0] result,
  input  [31:0] rs_addr,
  input  [31:0] rt_addr,
  input  [31:0] rd_addr,
  input  [31:0] tnew,
  input  [31:0] preserved0,
  input  [31:0] preserved1,
  input  [31:0] preserved2,
  input  [31:0] preserved3,
  input  [31:0] preserved4,
  input  enable,
  input  clk,
  input  reset,
  output [31:0] PC_2,
  output [31:0] PC4_2,
  output [31:0] instruction_2,
  output [31:0] rs_value_2,
  output [31:0] rt_value_2,
  output [31:0] immediate_2,
  output [31:0] result_2,
  output [31:0] rs_addr_2,
  output [31:0] rt_addr_2,
  output [31:0] rd_addr_2,
  output [31:0] tnew_2,
  output [31:0] preserved0_2,
  output [31:0] preserved1_2,
  output [31:0] preserved2_2,
  output [31:0] preserved3_2,
  output [31:0] preserved4_2
);

  wire not_1_out, or_1_out;
  wire [31:0] and_1_out, and_2_out, and_3_out, and_4_out, and_5_out, and_6_out, and_7_out, and_8_out,
       and_9_out, and_10_out, and_11_out, and_12_out, and_13_out, and_14_out, and_15_out, and_16_out,
       bit_extender_1_out;

  assign and_1_out = PC & bit_extender_1_out;  // AND_Gate and_1, 32 bits wide
  assign and_2_out = PC4 & bit_extender_1_out;  // AND_Gate and_2, 32 bits wide
  assign and_3_out = instruction & bit_extender_1_out;  // AND_Gate and_3, 32 bits wide
  assign and_4_out = rs_value & bit_extender_1_out;  // AND_Gate and_4, 32 bits wide
  assign and_5_out = rt_value & bit_extender_1_out;  // AND_Gate and_5, 32 bits wide
  assign and_6_out = immediate & bit_extender_1_out;  // AND_Gate and_6, 32 bits wide
  assign and_7_out = result & bit_extender_1_out;  // AND_Gate and_7, 32 bits wide
  assign and_8_out = rs_addr & bit_extender_1_out;  // AND_Gate and_8, 32 bits wide
  assign and_9_out = rt_addr & bit_extender_1_out;  // AND_Gate and_9, 32 bits wide
  assign and_10_out = rd_addr & bit_extender_1_out;  // AND_Gate and_10, 32 bits wide
  assign and_11_out = tnew & bit_extender_1_out;  // AND_Gate and_11, 32 bits wide
  assign and_12_out = preserved0 & bit_extender_1_out;  // AND_Gate and_12, 32 bits wide
  assign and_13_out = preserved1 & bit_extender_1_out;  // AND_Gate and_13, 32 bits wide
  assign and_14_out = preserved2 & bit_extender_1_out;  // AND_Gate and_14, 32 bits wide
  assign and_15_out = preserved3 & bit_extender_1_out;  // AND_Gate and_15, 32 bits wide
  assign and_16_out = preserved4 & bit_extender_1_out;  // AND_Gate and_16, 32 bits wide
  or or_1 (or_1_out, enable, reset);
  Register #(.width(32)) register_1 (.D(and_1_out), .en(or_1_out), .Q(PC_2), .clk(clk));  // open: clr
  Register #(.width(32)) register_2 (.D(and_2_out), .en(or_1_out), .Q(PC4_2), .clk(clk));  // open: clr
  Register #(.width(32)) register_3 (.D(and_3_out), .en(or_1_out), .Q(instruction_2), .clk(clk));  // open: clr
  Register #(.width(32)) register_4 (.D(and_4_out), .en(or_1_out), .Q(rs_value_2), .clk(clk));  // open: clr
  Register #(.width(32)) register_5 (.D(and_5_out), .en(or_1_out), .Q(rt_value_2), .clk(clk));  // open: clr
  Register #(.width(32)) register_6 (.D(and_6_out), .en(or_1_out), .Q(immediate_2), .clk(clk));  // open: clr
  Register #(.width(32)) register_7 (.D(and_7_out), .en(or_1_out), .Q(result_2), .clk(clk));  // open: clr
  Register #(.width(32)) register_8 (.D(and_8_out), .en(or_1_out), .Q(rs_addr_2), .clk(clk));  // open: clr
  Register #(.width(32)) register_9 (.D(and_9_out), .en(or_1_out), .Q(rt_addr_2), .clk(clk));  // open: clr
  Register #(.width(32)) register_10 (.D(and_10_out), .en(or_1_out), .Q(rd_addr_2), .clk(clk));  // open: clr
  Register #(.width(32)) register_11 (.D(and_11_out), .en(or_1_out), .Q(tnew_2), .clk(clk));  // open: clr
  Register #(.width(32)) register_12 (.D(and_12_out), .en(or_1_out), .Q(preserved0_2), .clk(clk));  // open: clr
  Register #(.width(32)) register_13 (.D(and_13_out), .en(or_1_out), .Q(preserved1_2), .clk(clk));  // open: clr
  Register #(.width(32)) register_14 (.D(and_14_out), .en(or_1_out), .Q(preserved2_2), .clk(clk));  // open: clr
  Register #(.width(32)) register_15 (.D(and_15_out), .en(or_1_out), .Q(preserved3_2), .clk(clk));  // open: clr
  Register #(.width(32)) register_16 (.D(and_16_out), .en(or_1_out), .Q(preserved4_2), .clk(clk));  // open: clr
  not not_1 (not_1_out, reset);
  assign bit_extender_1_out = {{31{not_1_out}}, not_1_out};  // Bit_Extender bit_extender_1
endmodule

module RDecoder (
  input  [31:0] instruction,
  output [31:0] rd
);

  wire [4:0] wb_1_grf_write_address;
  wire [31:0] shifter_1_out;
  wire [31:31] wb_1_ctrl_grf_write;

  WB wb_1 (
    .instruction(instruction), .ctrl_GRF_write(wb_1_ctrl_grf_write[31]),
    .GRF_write_address(wb_1_grf_write_address));
  assign rd = {{31{wb_1_ctrl_grf_write[31]}}, 1'b0} & shifter_1_out;  // AND_Gate and_1, 32 bits wide
  Shifter #(.width(32)) shifter_1 (.in(32'h1), .\dist (wb_1_grf_write_address), .out(shifter_1_out));
endmodule

module rs_used_decoder (
  input  [31:0] instruction,
  output rs_used
);

  wire instruction_decoder_1_addu, instruction_decoder_1_beq, instruction_decoder_1_jr,
       instruction_decoder_1_lw, instruction_decoder_1_ori, instruction_decoder_1_subu,
       instruction_decoder_1_sw;

  instruction_decoder instruction_decoder_1 (
    .opcode(instruction[31:26]), .funct(instruction[5:0]), .addu(instruction_decoder_1_addu),
    .subu(instruction_decoder_1_subu), .ori(instruction_decoder_1_ori), .lw(instruction_decoder_1_lw),
    .sw(instruction_decoder_1_sw), .beq(instruction_decoder_1_beq), .jr(instruction_decoder_1_jr));  // open: lui, j, jal
  or or_1 (rs_used, instruction_decoder_1_addu, instruction_decoder_1_subu, instruction_decoder_1_ori, instruction_decoder_1_lw, instruction_decoder_1_sw, instruction_decoder_1_beq, instruction_decoder_1_jr);

  // Notes on the sheet:
  //   opcode
  //   funct
endmodule

module rt_used_decoder (
  input  [31:0] instruction,
  output rt_used
);

  wire instruction_decoder_1_addu, instruction_decoder_1_beq, instruction_decoder_1_subu,
       instruction_decoder_1_sw;

  instruction_decoder instruction_decoder_1 (
    .opcode(instruction[31:26]), .funct(instruction[5:0]), .addu(instruction_decoder_1_addu),
    .subu(instruction_decoder_1_subu), .sw(instruction_decoder_1_sw), .beq(instruction_decoder_1_beq));  // open: ori, lui, lw, j, jal, jr
  or or_1 (rt_used, instruction_decoder_1_addu, instruction_decoder_1_subu, instruction_decoder_1_sw, instruction_decoder_1_beq);

  // Notes on the sheet:
  //   opcode
  //   funct
endmodule

module RSDecoder (
  input  [31:0] instruction,
  output [31:0] rs
);

  wire [31:0] shifter_1_out;
  wire [31:31] rs_used_decoder_1_rs_used;

  rs_used_decoder rs_used_decoder_1 (.instruction(instruction), .rs_used(rs_used_decoder_1_rs_used[31]));
  Shifter #(.width(32)) shifter_1 (.in(32'h1), .\dist (instruction[25:21]), .out(shifter_1_out));
  assign rs = {32{rs_used_decoder_1_rs_used[31]}} & shifter_1_out;  // AND_Gate and_1, 32 bits wide

  // Notes on the sheet:
  //   rs
endmodule

module RTDecoder (
  input  [31:0] instruction,
  output [31:0] rt
);

  wire [31:0] shifter_1_out;
  wire [31:31] rt_used_decoder_1_rt_used;

  rt_used_decoder rt_used_decoder_1 (.instruction(instruction), .rt_used(rt_used_decoder_1_rt_used[31]));
  Shifter #(.width(32)) shifter_1 (.in(32'h1), .\dist (instruction[20:16]), .out(shifter_1_out));
  assign rt = {32{rt_used_decoder_1_rt_used[31]}} & shifter_1_out;  // AND_Gate and_1, 32 bits wide

  // Notes on the sheet:
  //   rt
endmodule

module forwardor (
  input  [31:0] priority0_value,
  input  [31:0] priority0_tnew,
  input  [31:0] address,
  input  [31:0] priority0_address,
  input  [31:0] priority1_value,
  input  [31:0] priority1_tnew,
  input  [31:0] priority1_address,
  input  [31:0] priority2_value,
  input  [31:0] priority2_tnew,
  input  [31:0] priority2_address,
  input  [31:0] fallback,
  output [31:0] forwarded
);

  wire forward_backbone_1_selected_2, forward_backbone_2_selected_2, forward_backbone_3_selected_2;

  forward_backbone forward_backbone_1 (
    .tnew(priority0_tnew), .address(priority0_address), .target_address(address), .value(priority0_value),
    .forwarded_value(forwarded), .selected_2(forward_backbone_1_selected_2));  // open: selected
  forward_backbone forward_backbone_2 (
    .tnew(priority1_tnew), .address(priority1_address), .target_address(address), .value(priority1_value),
    .forwarded_value(forwarded), .selected(forward_backbone_1_selected_2),
    .selected_2(forward_backbone_2_selected_2));
  forward_backbone forward_backbone_3 (
    .tnew(priority2_tnew), .address(priority2_address), .target_address(address), .value(priority2_value),
    .forwarded_value(forwarded), .selected(forward_backbone_2_selected_2),
    .selected_2(forward_backbone_3_selected_2));
  forward_backbone forward_backbone_4 (
    .tnew({32{1'b0}}), .address(address), .target_address(address), .value(fallback),
    .forwarded_value(forwarded), .selected(forward_backbone_3_selected_2));  // open: selected_2

  // Notes on the sheet:
  //   priority0_value: pull=up
  //   priority1_tnew: pull=up
  //   priority2_address: pull=up
  //   priority1_address: pull=up
  //   priority0_address: pull=up
  //   priority1_value: pull=up
  //   priority2_value: pull=up
  //   priority0_tnew: pull=up
  //   priority2_tnew: pull=up
endmodule

module forwardor_backbone (
  input  [31:0] priority0_address,
  input  [31:0] priority0_value,
  input  [31:0] priority0_tnew,
  input  [31:0] target_address,
  input  [31:0] priority1_value,
  input  [31:0] priority1_tnew,
  input  [31:0] priority1_address,
  output [31:0] forwarded_value,
  output [31:0] forwarded_tnew,
  output [31:0] forwarded_address
);

  wire not_1_out, priority0_address_match, priority0_available, priority0_ok, priority1_address_match,
       priority1_available, priority1_ok;

  not not_1 (not_1_out, priority0_ok);
  and and_1 (priority0_ok, priority0_address_match, priority0_available);
  and and_2 (priority1_ok, priority1_address_match, not_1_out, priority1_available);
  assign forwarded_value = priority0_ok ? priority0_value : 32'bz;  // Controlled_Buffer controlled_buffer_1
  assign forwarded_value = priority1_ok ? priority1_value : 32'bz;  // Controlled_Buffer controlled_buffer_2
  Comparator #(.width(32), .mode("unsigned")) comparator_1 (
    .a(priority0_tnew), .b({32{1'b0}}), .eq(priority0_available));  // open: gt, lt
  Comparator #(.width(32), .mode("unsigned")) comparator_2 (
    .a({32{1'b0}}), .b(priority1_tnew), .eq(priority1_available));  // open: gt, lt
  assign forwarded_tnew = priority0_ok ? priority0_tnew : 32'bz;  // Controlled_Buffer controlled_buffer_3
  assign forwarded_tnew = priority1_ok ? priority1_tnew : 32'bz;  // Controlled_Buffer controlled_buffer_4
  Comparator #(.width(32), .mode("unsigned")) comparator_3 (
    .a(priority0_address), .b(target_address), .eq(priority0_address_match));  // open: gt, lt
  Comparator #(.width(32), .mode("unsigned")) comparator_4 (
    .a(target_address), .b(priority1_address), .eq(priority1_address_match));  // open: gt, lt
  assign forwarded_address = priority0_ok ? priority0_address : 32'bz;  // Controlled_Buffer controlled_buffer_5
  assign forwarded_address = priority1_ok ? priority1_address : 32'bz;  // Controlled_Buffer controlled_buffer_6
endmodule

module forward_backbone (
  input  selected,
  input  [31:0] tnew,
  input  [31:0] address,
  input  [31:0] target_address,
  input  [31:0] value,
  output selected_2,
  output [31:0] forwarded_value
);

  wire address_match, and_1_out, available, not_1_out;

  or or_1 (selected_2, selected, and_1_out);
  and and_1 (and_1_out, available, not_1_out, address_match);
  not not_1 (not_1_out, selected);
  assign forwarded_value = and_1_out ? value : 32'bz;  // Controlled_Buffer controlled_buffer_1
  Comparator #(.width(32), .mode("unsigned")) comparator_1 (
    .a(address), .b(target_address), .eq(address_match));  // open: gt, lt
  Comparator #(.width(32), .mode("unsigned")) comparator_2 (.a(tnew), .b({32{1'b0}}), .eq(available));  // open: gt, lt

  // Notes on the sheet:
  //   selected: pull=down
endmodule

module pauser (
  input  [31:0] tnew1,
  input  [31:0] waddr1,
  input  [31:0] instruction,
  input  [31:0] tnew2,
  input  [31:0] waddr2,
  output pause
);

  wire and_5_out, and_6_out, and_7_out, and_8_out, comparator_1_gt, comparator_2_gt, comparator_3_gt,
       comparator_4_gt, comparator_5_gt, comparator_6_gt, comparator_7_gt, comparator_8_gt;
  wire [31:0] and_1_out, and_2_out, and_3_out, and_4_out, rs_tuse_decoder_1_rs_tuse,
       rs_tuse_decoder_2_rs_tuse, rsdecoder_1_rs, rsdecoder_2_rs, rt_tuse_decoder_1_rs_tuse,
       rt_tuse_decoder_2_rs_tuse, rtdecoder_1_rt, rtdecoder_2_rt;

  rs_tuse_decoder rs_tuse_decoder_1 (.instruction(instruction), .rs_tuse(rs_tuse_decoder_1_rs_tuse));
  RSDecoder rsdecoder_1 (.instruction(instruction), .rs(rsdecoder_1_rs));
  rt_tuse_decoder rt_tuse_decoder_1 (.instruction(instruction), .rs_tuse(rt_tuse_decoder_1_rs_tuse));
  RTDecoder rtdecoder_1 (.instruction(instruction), .rt(rtdecoder_1_rt));
  rs_tuse_decoder rs_tuse_decoder_2 (.instruction(instruction), .rs_tuse(rs_tuse_decoder_2_rs_tuse));
  RSDecoder rsdecoder_2 (.instruction(instruction), .rs(rsdecoder_2_rs));
  rt_tuse_decoder rt_tuse_decoder_2 (.instruction(instruction), .rs_tuse(rt_tuse_decoder_2_rs_tuse));
  RTDecoder rtdecoder_2 (.instruction(instruction), .rt(rtdecoder_2_rt));
  assign and_1_out = rsdecoder_1_rs & waddr1;  // AND_Gate and_1, 32 bits wide
  assign and_2_out = rtdecoder_1_rt & waddr1;  // AND_Gate and_2, 32 bits wide
  assign and_3_out = rsdecoder_2_rs & waddr2;  // AND_Gate and_3, 32 bits wide
  assign and_4_out = rtdecoder_2_rt & waddr2;  // AND_Gate and_4, 32 bits wide
  Comparator #(.width(32), .mode("unsigned")) comparator_1 (
    .a(tnew1), .b(rs_tuse_decoder_1_rs_tuse), .gt(comparator_1_gt));  // open: eq, lt
  and and_5 (and_5_out, comparator_1_gt, comparator_2_gt);
  Comparator #(.width(32), .mode("unsigned")) comparator_2 (
    .a(and_1_out), .b({32{1'b0}}), .gt(comparator_2_gt));  // open: eq, lt
  Comparator #(.width(32), .mode("unsigned")) comparator_3 (
    .a(tnew1), .b(rt_tuse_decoder_1_rs_tuse), .gt(comparator_3_gt));  // open: eq, lt
  and and_6 (and_6_out, comparator_3_gt, comparator_4_gt);
  Comparator #(.width(32), .mode("unsigned")) comparator_4 (
    .a(and_2_out), .b({32{1'b0}}), .gt(comparator_4_gt));  // open: eq, lt
  Comparator #(.width(32), .mode("unsigned")) comparator_5 (
    .a(tnew2), .b(rs_tuse_decoder_2_rs_tuse), .gt(comparator_5_gt));  // open: eq, lt
  and and_7 (and_7_out, comparator_5_gt, comparator_6_gt);
  Comparator #(.width(32), .mode("unsigned")) comparator_6 (
    .a(and_3_out), .b({32{1'b0}}), .gt(comparator_6_gt));  // open: eq, lt
  Comparator #(.width(32), .mode("unsigned")) comparator_7 (
    .a(tnew2), .b(rt_tuse_decoder_2_rs_tuse), .gt(comparator_7_gt));  // open: eq, lt
  and and_8 (and_8_out, comparator_7_gt, comparator_8_gt);
  Comparator #(.width(32), .mode("unsigned")) comparator_8 (
    .a(and_4_out), .b({32{1'b0}}), .gt(comparator_8_gt));  // open: eq, lt
  or or_1 (pause, and_5_out, and_6_out, and_7_out, and_8_out);
endmodule

module rs_tuse_decoder (
  input  [31:0] instruction,
  output [31:0] rs_tuse
);

  wire instruction_decoder_1_beq, instruction_decoder_1_jr, rs_tuse_select;

  instruction_decoder instruction_decoder_1 (
    .opcode(instruction[31:26]), .funct(instruction[5:0]), .beq(instruction_decoder_1_beq),
    .jr(instruction_decoder_1_jr));  // open: addu, subu, ori, lui, lw, sw, j, jal
  or or_1 (rs_tuse_select, instruction_decoder_1_beq, instruction_decoder_1_jr);
  Multiplexer #(.width(32), .enable("false")) multiplexer_1 (
    .in0(32'h1), .in1({32{1'b0}}), .out(rs_tuse), .sel(rs_tuse_select));

  // Notes on the sheet:
  //   opcode
  //   funct
endmodule

module rt_tuse_decoder (
  input  [31:0] instruction,
  output [31:0] rs_tuse
);

  wire instruction_decoder_1_addu, instruction_decoder_1_beq, instruction_decoder_1_j,
       instruction_decoder_1_jal, instruction_decoder_1_jr, instruction_decoder_1_lui,
       instruction_decoder_1_lw, instruction_decoder_1_ori, instruction_decoder_1_subu,
       instruction_decoder_1_sw;
  wire [1:0] rt_tuse_select;

  instruction_decoder instruction_decoder_1 (
    .opcode(instruction[31:26]), .funct(instruction[5:0]), .addu(instruction_decoder_1_addu),
    .subu(instruction_decoder_1_subu), .ori(instruction_decoder_1_ori), .lui(instruction_decoder_1_lui),
    .lw(instruction_decoder_1_lw), .sw(instruction_decoder_1_sw), .beq(instruction_decoder_1_beq),
    .j(instruction_decoder_1_j), .jal(instruction_decoder_1_jal), .jr(instruction_decoder_1_jr));
  buf or_1 (rt_tuse_select[1], instruction_decoder_1_sw);  // OR_Gate
  Multiplexer #(.select(2), .width(32), .enable("false")) multiplexer_1 (
    .in0(32'h1), .in1({32{1'b0}}), .in2(32'h2), .out(rs_tuse), .sel(rt_tuse_select));  // open: in3
  buf or_2 (rt_tuse_select[0], instruction_decoder_1_beq);  // OR_Gate

  // Notes on the sheet:
  //   opcode
  //   funct
endmodule

module tnew_decoder (
  input  [31:0] instruction,
  output [31:0] rs_tuse
);

  wire instruction_decoder_1_addu, instruction_decoder_1_beq, instruction_decoder_1_j,
       instruction_decoder_1_jal, instruction_decoder_1_jr, instruction_decoder_1_lui,
       instruction_decoder_1_lw, instruction_decoder_1_ori, instruction_decoder_1_subu,
       instruction_decoder_1_sw;
  wire [1:0] tnew_select;

  instruction_decoder instruction_decoder_1 (
    .opcode(instruction[31:26]), .funct(instruction[5:0]), .addu(instruction_decoder_1_addu),
    .subu(instruction_decoder_1_subu), .ori(instruction_decoder_1_ori), .lui(instruction_decoder_1_lui),
    .lw(instruction_decoder_1_lw), .sw(instruction_decoder_1_sw), .beq(instruction_decoder_1_beq),
    .j(instruction_decoder_1_j), .jal(instruction_decoder_1_jal), .jr(instruction_decoder_1_jr));
  buf or_1 (tnew_select[1], instruction_decoder_1_lw);  // OR_Gate
  Multiplexer #(.select(2), .width(32), .enable("false")) multiplexer_1 (
    .in0(32'h1), .in1({32{1'b0}}), .in2(32'h2), .out(rs_tuse), .sel(tnew_select));  // open: in3
  or or_2 (tnew_select[0], instruction_decoder_1_lui, instruction_decoder_1_jal);

  // Notes on the sheet:
  //   opcode
  //   funct
endmodule

module sub1 (
  input  [31:0] in_1,
  output [31:0] out_2
);

  wire comparator_1_gt;
  wire [31:0] bit_extender_1_out, subtractor_1_out;

  Subtractor #(.width(32)) subtractor_1 (.a(in_1), .b(32'h1), .out(subtractor_1_out));  // open: bin, bout
  assign bit_extender_1_out = {{31{comparator_1_gt}}, comparator_1_gt};  // Bit_Extender bit_extender_1
  Comparator #(.width(32)) comparator_1 (.a(in_1), .b({32{1'b0}}), .gt(comparator_1_gt));  // open: eq, lt
  assign out_2 = bit_extender_1_out & subtractor_1_out;  // AND_Gate and_1, 32 bits wide
endmodule
